// Digital circuit template_01.dig as structural Verilog
module template_01 (
  input  [3:0] in,
  output out
);

  wire and_1_out, and_2_out, and_3_out, and_4_out, not_1_out, not_2_out, not_3_out, not_4_out, not_5_out,
       not_6_out;

  and and_1 (and_1_out, in[3], in[1], not_1_out);
  not not_1 (not_1_out, in[0]);
  and and_2 (and_2_out, not_2_out, in[2], not_3_out);
  not not_2 (not_2_out, in[3]);
  not not_3 (not_3_out, in[1]);
  and and_3 (and_3_out, not_4_out, not_5_out, in[0]);
  not not_4 (not_4_out, in[3]);
  not not_5 (not_5_out, in[2]);
  and and_4 (and_4_out, not_6_out, in[0]);
  not not_6 (not_6_out, in[1]);
  or or_1 (out, and_1_out, and_2_out, and_3_out, and_4_out);

  // Other names for the same wires on the sheet: A = in[0]; B = in[1]; C = in[2]; D = in[3]
endmodule
