// Digital circuit template_02.dig as structural Verilog
module template_02 (
  input  [2:0] in0,
  input  [2:0] in1,
  input  addsubtract,
  output [2:0] out
);

  wire and_2_out, and_3_out, and_4_out, and_5_out, and_6_out, and_7_out, and_8_out, and_10_out, and_11_out,
       and_12_out, and_13_out, and_14_out, and_15_out, and_16_out, not_1_out, not_2_out, not_3_out,
       not_4_out, not_5_out, not_6_out, not_7_out;
  wire [2:0] add_1_s, sub_1_s, ut0, ut1;

  not not_1 (not_1_out, in0[2]);
  not not_2 (not_2_out, in0[1]);
  not not_3 (not_3_out, in0[0]);
  and and_1 (ut0[0], in0[2], in0[1], in0[0]);
  and and_2 (and_2_out, in0[2], not_2_out, in0[0]);
  and and_3 (and_3_out, in0[2], in0[1], not_3_out);
  and and_4 (and_4_out, not_1_out, in0[1], in0[0]);
  and and_5 (and_5_out, not_1_out, in0[1], in0[0]);
  and and_6 (and_6_out, in0[2], not_3_out);
  and and_7 (and_7_out, not_2_out, in0[0]);
  and and_8 (and_8_out, in0[1], not_3_out);
  or or_1 (ut0[1], and_2_out, and_3_out, and_4_out);
  or or_2 (ut0[2], and_5_out, and_6_out, and_7_out, and_8_out);
  not not_4 (not_4_out, addsubtract);
  not not_5 (not_5_out, in1[2]);
  Add #(.Bits(3)) add_1 (.a(ut0), .b(ut1), .c_i(not_4_out), .s(add_1_s));  // open: c_o
  not not_6 (not_6_out, in1[1]);
  Sub #(.Bits(3)) sub_1 (.a(ut0), .b(ut1), .c_i(addsubtract), .s(sub_1_s));  // open: c_o
  not not_7 (not_7_out, in1[0]);
  and and_9 (ut1[0], in1[2], in1[1], in1[0]);
  and and_10 (and_10_out, in1[2], not_6_out, in1[0]);
  and and_11 (and_11_out, in1[2], in1[1], not_7_out);
  and and_12 (and_12_out, not_5_out, in1[1], in1[0]);
  and and_13 (and_13_out, not_5_out, in1[1], in1[0]);
  and and_14 (and_14_out, in1[2], not_7_out);
  and and_15 (and_15_out, not_6_out, in1[0]);
  and and_16 (and_16_out, in1[1], not_7_out);
  or or_3 (ut1[1], and_10_out, and_11_out, and_12_out);
  or or_4 (ut1[2], and_13_out, and_14_out, and_15_out, and_16_out);
  assign out = add_1_s | sub_1_s;  // Or or_5, 3 bits wide

  // Other names for the same wires on the sheet: C = in0[0]; B = in0[1]; A = in0[2]; D = in1[0]; E = in1[1];
  //   F = in1[2]
endmodule
