// Digital circuit exam2_1.dig as structural Verilog
module exam2_1 (
  input  clk
);

  wire and_3_out, and_4_out, car, d_ff_3_q, d_ff_4_q, Gcar, Gpeople, multiplexer_1_out, multiplexer_2_out,
       nor_1_out, nor_2_out, or_1_out, or_2_out, or_3_out, or_4_out, people, Rcar, register_3_q,
       register_4_q, Rpeople, \wait , Ycar, Ypeople, Z1, Z2;

  nor nor_1 (nor_1_out, Ypeople, Rpeople, Gpeople);
  nor nor_2 (nor_2_out, Ycar, Rcar, Gcar);
  Multiplexer multiplexer_1 (.sel(Z1), .in_0(nor_1_out), .in_1(1'b0), .out(multiplexer_1_out));
  Multiplexer multiplexer_2 (.sel(Z2), .in_0(nor_2_out), .in_1(1'b0), .out(multiplexer_2_out));
  Register register_1 (.D(multiplexer_1_out), .C(clk), .en(1'b1), .Q(Z1));
  Register register_2 (.D(multiplexer_2_out), .C(clk), .en(1'b1), .Q(Z2));
  Register register_3 (.D(people), .C(clk), .en(1'b1), .Q(register_3_q));
  Register register_4 (.D(car), .C(clk), .en(1'b1), .Q(register_4_q));
  D_FF d_ff_1 (.D(register_4_q), .C(clk), .Q(Ypeople));  // open: nQ
  Button u_people (.out(people));
  Button u_car (.out(car));
  Button u_wait (.out(\wait ));
  D_FF d_ff_2 (.D(register_3_q), .C(clk), .Q(Ycar));  // open: nQ
  D_FF d_ff_3 (.D(Ycar), .C(clk), .Q(d_ff_3_q));  // open: nQ
  D_FF d_ff_4 (.D(Ypeople), .C(clk), .Q(d_ff_4_q));  // open: nQ
  or or_1 (or_1_out, Gpeople, d_ff_3_q);
  or or_2 (or_2_out, Gcar, d_ff_4_q);
  and and_1 (Rcar, ~Rpeople, or_1_out);  // And
  and and_2 (Rpeople, ~Rcar, or_2_out);  // And
  and and_3 (and_3_out, or_1_out, ~car);  // And
  and and_4 (and_4_out, or_2_out, ~people);  // And
  or or_3 (or_3_out, Ycar, Z1);
  or or_4 (or_4_out, Ypeople, Z2);
  D_FF d_ff_5 (.D(and_3_out), .C(clk), .Q(Gpeople));  // open: nQ
  D_FF d_ff_6 (.D(and_4_out), .C(clk), .Q(Gcar));  // open: nQ
  LED RedCar (.in(Rcar));
  LED YellowCar (.in(or_3_out));
  LED GreenCar (.in(Gcar));
  LED RedWalk (.in(Rpeople));
  LED YellowWalk (.in(or_4_out));
  LED GreenWalk (.in(Gpeople));
endmodule
