// Digital circuit template_01.dig as structural Verilog
module template_01 (
  input  reset,
  input  clk,
  output C,
  output B,
  output A
);

  wire a_n, and_1_out, and_2_out, and_3_out, and_4_out, and_5_out, and_6_out, and_9_out, and_10_out, b_n,
       c_n, not_1_out, not_2_out, not_3_out, not_4_out, or_1_out, or_2_out, or_3_out;

  not not_1 (not_1_out, reset);
  not not_2 (not_2_out, c_n);
  not not_3 (not_3_out, b_n);
  not not_4 (not_4_out, a_n);
  and and_1 (and_1_out, not_4_out, b_n, not_1_out);
  and and_2 (and_2_out, a_n, c_n, not_1_out);
  and and_3 (and_3_out, a_n, not_2_out, not_1_out);
  and and_4 (and_4_out, not_4_out, b_n, not_1_out);
  and and_5 (and_5_out, not_3_out, not_2_out, not_1_out);
  and and_6 (and_6_out, b_n, c_n, not_1_out);
  and and_7 (C, c_n, not_1_out);
  and and_8 (B, b_n, not_1_out);
  and and_9 (and_9_out, a_n, not_1_out);
  and and_10 (and_10_out, a_n, not_3_out, c_n);
  or or_1 (or_1_out, and_1_out, and_2_out);
  or or_2 (or_2_out, and_3_out, and_4_out);
  or or_3 (or_3_out, and_5_out, and_6_out);
  or or_4 (A, and_9_out, and_10_out);
  D_FF u_c_n (.D(or_1_out), .C(clk), .Q(c_n));  // open: nQ
  D_FF u_b_n (.D(or_2_out), .C(clk), .Q(b_n));  // open: nQ
  D_FF u_a_n (.D(or_3_out), .C(clk), .Q(a_n));  // open: nQ
endmodule

/* Test case TestCase:
clk reset C B A
0 0 0 0 0
0 1 0 0 0
1 1 0 0 0
0 0 0 0 0
1 0 0 0 1
0 0 0 0 1
1 0 0 1 1
0 0 0 1 1
1 0 0 1 0
0 0 0 1 0
1 0 1 1 0
0 0 1 1 0
1 0 1 1 1
0 0 1 1 1
1 0 1 0 1
0 0 1 0 1
1 0 1 0 0
0 0 1 0 0
1 0 0 0 0
0 0 0 0 0
1 0 0 0 1
0 0 0 0 1
1 0 0 1 1
0 0 0 1 1
1 0 0 1 0
0 0 0 1 0
1 0 1 1 0
0 0 1 1 0
1 0 1 1 1
0 0 1 1 1
1 0 1 0 1
0 0 1 0 1
1 0 1 0 0
0 0 1 0 0
*/
