// Digital circuit template_02.dig as structural Verilog
module template_02 (
  input  [15:0] A,
  input  Start,
  input  clk,
  output [15:0] sqrt,
  output busy
);

  wire undriven;
  wire [7:0] add_1_s, add_2_s, register_1_q, register_2_q;
  wire [15:0] mul_1_mul, mul_2_mul;

  Add #(.Bits(8)) add_1 (.a(register_1_q), .b(8'h1), .c_i(clk), .s(add_1_s));  // open: c_o
  Add #(.Bits(8)) add_2 (.a(register_2_q), .b(8'h1), .c_i(clk), .s(add_2_s));  // open: c_o
  Register #(.Bits(8)) register_1 (.D(add_1_s), .C(clk), .en(1'b1), .Q(register_1_q));
  Register #(.Bits(8)) register_2 (.D(add_2_s), .C(undriven), .en(1'b1), .Q(register_2_q));
  Mul #(.Bits(8)) mul_1 (.a(register_1_q), .b(register_1_q), .mul(mul_1_mul));
  Mul #(.Bits(8)) mul_2 (.a(register_2_q), .b(register_2_q), .mul(mul_2_mul));
  Comparator #(.Bits(16)) comparator_1 (.a(mul_1_mul), .b(A), .eq(busy));  // open: gt, lt
  Comparator #(.Bits(16)) comparator_2 (.a(mul_2_mul), .b(A));  // open: gt, eq, lt

  assign sqrt = A;
  // also tied to GND on the sheet: {register_1_q[1], register_1_q[2], register_1_q[3], register_1_q[4], register_1_q[5], register_1_q[6], register_1_q[7], register_2_q[1], register_2_q[2], register_2_q[3], register_2_q[4], register_2_q[5], register_2_q[6], register_2_q[7]}
  // also tied to VCC on the sheet: {register_1_q[0], register_2_q[0]}

  // Notes on the sheet:
  //   clk: Hz: 200
endmodule

/* Test case TestCase1:
clk A input sqrt busy
0 0 0 0 0
1 0 0 0 0
0 0 0 0 0
1 0 0 0 0
0 0 1 X X
1 0 1 X X
loop(x,1000)
0 0 0 X X
1 0 0 X X
end loop
0 0 0 0 0
1 0 0 0 0
*/

/* Test case TestCase2:
clk A input sqrt busy
0 0 0 0 0
1 0 0 0 0
0 0 0 0 0
1 0 0 0 0
0 1 1 X X
1 1 1 X X
loop(x,1000)
0 1 0 X X
1 1 0 X X
end loop
0 0 0 1 0
1 0 0 1 0
*/

/* Test case TestCase3:
clk A input sqrt busy
0 0 0 0 0
1 0 0 0 0
0 0 0 0 0
1 0 0 0 0
0 4 1 X X
1 4 1 X X
loop(x,1000)
0 4 0 X X
1 4 0 X X
end loop
0 0 0 2 0
1 0 0 2 0
*/

/* Test case TestCase4:
clk A input sqrt busy
0 0 0 0 0
1 0 0 0 0
0 0 0 0 0
1 0 0 0 0
0 9 1 X X
1 9 1 X X
loop(x,1000)
0 9 0 X X
1 9 0 X X
end loop
0 0 0 3 0
1 0 0 3 0
*/

/* Test case TestCase5:
clk A input sqrt busy
0 0 0 0 0
1 0 0 0 0
0 0 0 0 0
1 0 0 0 0
0 8 1 X X
1 8 1 X X
loop(x,1000)
0 8 0 X X
1 8 0 X X
end loop
0 0 0 2 0
1 0 0 2 0
*/
