// Digital circuit sort.dig as structural Verilog
module sort (
  input  clock,
  input  reset,
  input  [8:0] N,
  input  start,
  output [31:0] clockcount,
  output done,
  output [7:0] displayout,
  output valid
);

  wire and_1_out, and_3_out, clk, comparator_3_eq, comparator_4_eq, eq__0, or_2_out, output__eq__N, s2__eq,
       select_Addr, select_fetch, select_Input, select_Output;
  wire [8:0] add_1_s, AddrCount, CountNum, CountNum__plus__1, fetchCount, InputCount, multiplexer_1_out,
       multiplexer_2_out, multiplexer_4_out, OutputCount, RAM_d, ROMFILE_d, sub_1_s, sub_2_s;
  wire [8:8] driver_1_out;

  Comparator #(.Bits(9)) comparator_1 (.a(InputCount), .b(AddrCount), .eq(s2__eq));  // open: gt, lt
  Sub #(.Bits(9)) sub_1 (.a(N), .b(9'h1), .c_i(1'b0), .s(sub_1_s));  // open: c_o
  and and_1 (and_1_out, clock, start, ~output__eq__N);  // And
  Comparator #(.Bits(9)) comparator_2 (.a(OutputCount), .b(sub_1_s), .eq(output__eq__N));  // open: gt, lt
  or or_1 (clk, and_1_out, reset);
  // Probe on InputCount
  ROM #(.AddrBits(9), .isProgramMemory("true"), .Bits(9)) ROMFILE (.A(InputCount), .sel(select_Input), .D(ROMFILE_d));
  Comparator #(.Bits(9)) comparator_3 (.a(OutputCount), .b(N), .eq(comparator_3_eq));  // open: gt, lt
  Multiplexer #(.Bits(9)) multiplexer_1 (
    .sel(select_Input), .in_0(fetchCount), .in_1(ROMFILE_d), .out(multiplexer_1_out));
  Sub #(.Bits(9)) sub_2 (.a(CountNum), .b(9'h1), .c_i(1'b0), .s(sub_2_s));  // open: c_o
  // Probe on fetchCount
  Comparator #(.Bits(9)) comparator_4 (.a(InputCount), .b(N), .eq(comparator_4_eq));  // open: gt, lt
  and and_2 (select_Addr, ~select_Input, ~eq__0);  // And
  and and_3 (and_3_out, ~select_Input, eq__0);  // And
  Comparator #(.Bits(9)) comparator_5 (.a(CountNum), .b({9{1'b0}}), .eq(eq__0));  // open: gt, lt
  Multiplexer #(.Bits(9)) multiplexer_2 (.sel(eq__0), .in_0(sub_2_s), .in_1(CountNum), .out(multiplexer_2_out));
  Add #(.Bits(9)) add_1 (.a(CountNum), .b(9'h1), .c_i(1'b0), .s(add_1_s));  // open: c_o
  not not_1 (select_Input, comparator_4_eq);
  and and_4 (select_Output, ~comparator_3_eq, ~select_Input, ~select_fetch, ~select_Addr);  // And
  RAMDualPort #(.AddrBits(9), .Bits(9)) C (
    .A(multiplexer_1_out), .Din(CountNum__plus__1), .str(1'b1), .C(clk), .ld(1'b1), .D(CountNum));
  Multiplexer #(.Bits(9)) multiplexer_3 (
    .sel(select_Input), .in_0(multiplexer_2_out), .in_1(add_1_s), .out(CountNum__plus__1));
  and and_5 (select_fetch, and_3_out, ~s2__eq);  // And
  // Probe on CountNum
  // Probe on CountNum__plus__1
  Multiplexer #(.Bits(9)) multiplexer_4 (.sel(done), .in_0(AddrCount), .in_1(OutputCount), .out(multiplexer_4_out));
  or or_2 (or_2_out, select_Addr, done);
  Counter #(.Bits(9)) inputCounter (.en(select_Input), .C(clk), .clr(reset), .out(InputCount));  // open: ovf
  Counter #(.Bits(9)) counter_1 (.en(select_fetch), .C(clk), .clr(reset), .out(fetchCount));  // open: ovf
  nor nor_1 (done, ~start, select_Input, select_Addr, select_fetch);  // NOr
  RAMDualPort #(.AddrBits(9), .Bits(9)) RAM (
    .A(multiplexer_4_out), .Din(fetchCount), .str(select_Addr), .C(clk), .ld(or_2_out), .D(RAM_d));
  // Probe on InputCount
  // Probe on fetchCount
  // Probe on RAM_d
  assign {driver_1_out[8], displayout} = done ? RAM_d : 9'bz;  // Driver driver_1
  Seven_Seg_Hex seven_seg_hex_1 (.d(displayout[7:4]), .dp(1'b0));
  Counter #(.Bits(9)) resultAddress (.en(select_Addr), .C(clk), .clr(reset), .out(AddrCount));  // open: ovf
  Counter #(.Bits(9)) outputCounter (.en(select_Output), .C(clk), .clr(reset), .out(OutputCount));  // open: ovf
  Counter #(.Bits(32)) ClockCounting (.en(clk), .C(clk), .clr(reset), .out(clockcount));  // open: ovf
  Seven_Seg_Hex seven_seg_hex_2 (.d(displayout[3:0]), .dp(1'b0));
  // Probe on AddrCount
  // Probe on OutputCount

  assign valid = done;

  // Notes on the sheet:
  //   clock: Hz: 100
  //   N: default 511
  //   contents of ROMFILE (hex, n*v repeats v):
  //   1,4,2,3,7*0,42,21,59,19,25,30,0,13,c
endmodule
